# Fritzing sketch Untitled Sketch (saved by Fritzing 0.9.1b)
breadboards: 1

parts:
  IC1 = Dual Op-Amp [package=dip08]
  R1 = Resistor [tolerance=±5% resistance=100k package=THT]
  R2 = Resistor [tolerance=±5% resistance=100k package=THT]
  R3 = Resistor [tolerance=±5% resistance=100k package=THT]
  R4 = Resistor [tolerance=±5% resistance=100k package=THT]

nets:
  N1: IC1.A_-IN, R1.Pin_1, R2.Pin_1, R3.Pin_1, R4.Pin_1
